// Logisim project 32bit-Mips-ISA.circ as structural Verilog: 7 circuits, main circuit 1 bit ALU
module _1_bit_ALU (
  input  B,
  input  A,
  input  Carry_In,
  input  [2:0] in_4,
  input  Less,
  output out_6,
  output out_7,
  output Set
);

  wire AND_out, multiplexer_1_out, not_1_out, OR_out;

  Multiplexer multiplexer_1 (.in0(B), .in1(not_1_out), .out(multiplexer_1_out), .sel(in_4[2]));  // open: en
  not not_1 (not_1_out, B);
  Adder #(.width(1)) adder_1 (.a(A), .b(multiplexer_1_out), .out(Set), .cin(Carry_In), .cout(out_7));
  and AND (AND_out, A, B);
  or OR (OR_out, A, B);
  Multiplexer #(.select(2), .enable("false")) multiplexer_2 (
    .in0(AND_out), .in1(OR_out), .in2(Set), .in3(Less), .out(out_6), .sel(in_4[1:0]));
endmodule

// Control Unit
module Main_Control (
  input  [5:0] Opcode,
  output RegDest,
  output AluSrc,
  output MemtoReg,
  output RegWrite,
  output MemRead,
  output MemWrite,
  output beq,
  output bne,
  output jump,
  output [1:0] ALUOp
);

  wire not_1_out, not_2_out, not_3_out, not_4_out, not_5_out, not_6_out, not_7_out, not_8_out, not_9_out,
       not_10_out, not_11_out, not_12_out, not_13_out, not_14_out, not_15_out, not_16_out, not_17_out,
       not_18_out, not_19_out, not_20_out, not_21_out, not_22_out, not_23_out, not_24_out, not_25_out,
       or_2_out, or_3_out;

  not not_1 (not_1_out, Opcode[5]);
  not not_2 (not_2_out, Opcode[3]);
  not not_3 (not_3_out, Opcode[2]);
  not not_4 (not_4_out, Opcode[4]);
  not not_5 (not_5_out, Opcode[1]);
  and R_Format (ALUOp[1], not_1_out, not_4_out, not_2_out, not_3_out, not_5_out, not_7_out);
  not not_6 (not_6_out, Opcode[2]);
  not not_7 (not_7_out, Opcode[0]);
  not not_8 (not_8_out, Opcode[3]);
  not not_9 (not_9_out, Opcode[4]);
  and lw (MemRead, Opcode[5], not_9_out, not_8_out, not_6_out, Opcode[1], Opcode[0]);
  not not_10 (not_10_out, Opcode[4]);
  and sw (MemWrite, Opcode[5], not_10_out, Opcode[3], not_11_out, Opcode[1], Opcode[0]);
  not not_11 (not_11_out, Opcode[2]);
  not not_12 (not_12_out, Opcode[5]);
  not not_13 (not_13_out, Opcode[3]);
  not not_14 (not_14_out, Opcode[4]);
  not not_15 (not_15_out, Opcode[0]);
  not not_16 (not_16_out, Opcode[1]);
  not not_17 (not_17_out, Opcode[5]);
  not not_18 (not_18_out, Opcode[4]);
  and u_beq (beq, not_12_out, not_14_out, not_13_out, Opcode[2], not_16_out, not_15_out);
  not not_19 (not_19_out, Opcode[5]);
  not not_20 (not_20_out, Opcode[3]);
  not not_21 (not_21_out, Opcode[1]);
  and u_bne (bne, not_17_out, not_18_out, not_20_out, Opcode[2], not_21_out, Opcode[0]);
  not not_22 (not_22_out, Opcode[3]);
  not not_23 (not_23_out, Opcode[0]);
  not not_24 (not_24_out, Opcode[2]);
  not not_25 (not_25_out, Opcode[4]);
  and u_jump (jump, not_19_out, not_25_out, not_22_out, not_24_out, Opcode[1], not_23_out);
  or or_1 (ALUOp[0], bne, beq);
  or or_2 (or_2_out, ALUOp[1], bne, beq);
  or or_3 (or_3_out, MemWrite, bne, beq);
  not not_26 (AluSrc, or_2_out);
  not not_27 (RegWrite, or_3_out);

  assign MemtoReg = MemRead;
  assign RegDest = ALUOp[1];
endmodule

module CPU (
  output [29:0] Immediate_Value
);

  wire clock_1_out, Main_Control_alusrc, Main_Control_beq, Main_Control_bne, Main_Control_jump,
       Main_Control_memread, Main_Control_memtoreg, Main_Control_memwrite, Main_Control_regdest,
       Main_Control_regwrite, n32_bit_alu_32x1_1_out_6, Next_PC_pcsrc;
  wire [1:0] Main_Control_aluop;
  wire [2:0] ALU_Control_alucontrol;
  wire [4:0] multiplexer_2_out;
  wire [29:0] bit_extender_2_out, multiplexer_1_out, Next_PC_target_address;
  wire [31:0] adder_1_out, bit_extender_1_out, bit_extender_3_out, multiplexer_3_out, multiplexer_4_out,
       n32_bit_alu_32x1_1_out_5, PC_q, ram_1_data, Register_File_src_a, Register_File_src_b, rom_1_data;

  Clock clock_1 (.out(clock_1_out));
  Multiplexer #(.width(30)) multiplexer_1 (
    .in0(Immediate_Value), .in1(Next_PC_target_address), .out(multiplexer_1_out), .sel(Next_PC_pcsrc));  // open: en
  assign bit_extender_1_out = {{2{1'b0}}, multiplexer_1_out};  // Bit_Extender bit_extender_1
  Adder #(.width(32)) adder_1 (.a(bit_extender_1_out), .b({32{1'b0}}), .out(adder_1_out));  // open: cin, cout
  Register #(.width(32)) PC (.D(adder_1_out), .Q(PC_q), .clk(clock_1_out));  // open: en, clr
  Bit_Extender #(.in_width(32), .out_width(30)) bit_extender_2 (.in(PC_q), .out(bit_extender_2_out));
  Adder #(.width(30)) adder_2 (.a(30'h4), .b(bit_extender_2_out), .out(Immediate_Value));  // open: cin, cout
  ROM #(.addrWidth(24), .dataWidth(32)) rom_1 (.addr(PC_q[23:0]), .data(rom_1_data));  // open: sel
  Main_Control Main_Control (
    .Opcode(rom_1_data[31:26]), .RegDest(Main_Control_regdest), .AluSrc(Main_Control_alusrc),
    .MemtoReg(Main_Control_memtoreg), .RegWrite(Main_Control_regwrite), .MemRead(Main_Control_memread),
    .MemWrite(Main_Control_memwrite), .beq(Main_Control_beq), .ALUOp(Main_Control_aluop),
    .bne(Main_Control_bne), .jump(Main_Control_jump));
  Register_File Register_File (
    .Reg_1(rom_1_data[25:21]), .Src_A(Register_File_src_a), .Src_B(Register_File_src_b),
    .Reg_2(rom_1_data[20:16]), .Write_Reg(multiplexer_2_out), .RegWrite(Main_Control_regwrite),
    .Write_Data(multiplexer_4_out), .Clock(clock_1_out));
  assign bit_extender_3_out = {{16{rom_1_data[15]}}, rom_1_data[15:0]};  // Bit_Extender bit_extender_3
  Multiplexer #(.width(5)) multiplexer_2 (
    .in0(rom_1_data[20:16]), .in1(rom_1_data[15:11]), .out(multiplexer_2_out), .sel(Main_Control_regdest));  // open: en
  Multiplexer #(.width(32)) multiplexer_3 (
    .in0(Register_File_src_b), .in1(bit_extender_3_out), .out(multiplexer_3_out), .sel(Main_Control_alusrc));  // open: en
  Next_PC Next_PC (
    .Inc_PC(Immediate_Value), .Imm_26(rom_1_data[25:0]), .beq(Main_Control_beq), .bne(Main_Control_bne),
    .jump(Main_Control_jump), .Target_Address(Next_PC_target_address), .PCSrc(Next_PC_pcsrc),
    .zero(n32_bit_alu_32x1_1_out_6));
  ALU_Control ALU_Control (.ALUOp(Main_Control_aluop), .Func(rom_1_data[4:0]), .AluControl(ALU_Control_alucontrol));
  _32_bit_ALU_32x1 u_32_bit_alu_32x1_1 (
    .in_3(multiplexer_3_out), .in_4(Register_File_src_a), .out_5(n32_bit_alu_32x1_1_out_5),
    .out_6(n32_bit_alu_32x1_1_out_6), .in_2(ALU_Control_alucontrol));  // open: in_1, out_7, out_8
  RAM #(.addrWidth(24), .dataWidth(32), .bus("separate")) ram_1 (
    .addr(n32_bit_alu_32x1_1_out_5[23:0]), .din(Register_File_src_b), .data(ram_1_data),
    .str(Main_Control_memwrite), .clk(clock_1_out), .ld(Main_Control_memread));  // open: sel, clr
  Multiplexer #(.width(32)) multiplexer_4 (
    .in0(n32_bit_alu_32x1_1_out_5), .in1(ram_1_data), .out(multiplexer_4_out), .sel(Main_Control_memtoreg));  // open: en

  // Notes on the sheet:
  //   Instruction Memory
  //   0-25
  //   contents of rom_1 (hex, n*v repeats v):
  //   20080001 0 0 0 200a0064 0 0 0 1294822 0 0 0 1284820 0 0 0 ac290000 0 0 0 152afff4 0 0 0 8c2b0000 0 0
  //   0 16b5820 0 0 0 ac2b0001
  //   0-5
  //   0-15
  //   16-20
  //   21-25
  //   26-31
  //   16-20
  //   11-15
  //   Data Memory
endmodule

module Register_File (
  input  [31:0] Write_Data,
  input  RegWrite,
  input  Clock,
  input  [4:0] Reg_1,
  input  [4:0] Write_Reg,
  input  [4:0] Reg_2,
  output [31:0] Src_A,
  output [31:0] Src_B
);

  wire and_1_out, and_2_out, and_3_out, and_4_out, and_5_out, and_6_out, and_7_out, and_8_out, and_9_out,
       and_10_out, and_11_out, and_12_out, and_13_out, and_14_out, and_15_out, and_16_out, and_17_out,
       and_18_out, and_19_out, and_20_out, and_21_out, and_22_out, and_23_out, and_24_out, and_25_out,
       and_26_out, and_27_out, and_28_out, and_29_out, and_30_out, and_31_out, and_32_out, decoder_1_out0,
       decoder_1_out1, decoder_1_out2, decoder_1_out3, decoder_1_out4, decoder_1_out5, decoder_1_out6,
       decoder_1_out7, decoder_1_out8, decoder_1_out9, decoder_1_out10, decoder_1_out11, decoder_1_out12,
       decoder_1_out13, decoder_1_out14, decoder_1_out15, decoder_1_out16, decoder_1_out17, decoder_1_out18,
       decoder_1_out19, decoder_1_out20, decoder_1_out21, decoder_1_out22, decoder_1_out23, decoder_1_out24,
       decoder_1_out25, decoder_1_out26, decoder_1_out27, decoder_1_out28, decoder_1_out29, decoder_1_out30,
       decoder_1_out31;
  wire [31:0] a0_q, a1_q, a2_q, a3_q, at_q, fp_q, gp_q, k0_q, k1_q, ra_q, s0_q, s1_q, s2_q, s3_q, s4_q, s5_q,
       s6_q, s7_q, sp_q, t0_q, t1_q, t2_q, t3_q, t4_q, t5_q, t6_q, t7_q, t8_q, t9_q, v0_q, v1_q, zero_q;

  Decoder #(.select(5)) decoder_1 (
    .out0(decoder_1_out0), .out1(decoder_1_out1), .out2(decoder_1_out2), .out3(decoder_1_out3),
    .out4(decoder_1_out4), .out5(decoder_1_out5), .out6(decoder_1_out6), .out7(decoder_1_out7),
    .out8(decoder_1_out8), .out9(decoder_1_out9), .out10(decoder_1_out10), .out11(decoder_1_out11),
    .out12(decoder_1_out12), .out13(decoder_1_out13), .out14(decoder_1_out14), .out15(decoder_1_out15),
    .out16(decoder_1_out16), .out17(decoder_1_out17), .out18(decoder_1_out18), .out19(decoder_1_out19),
    .out20(decoder_1_out20), .out21(decoder_1_out21), .out22(decoder_1_out22), .out23(decoder_1_out23),
    .out24(decoder_1_out24), .out25(decoder_1_out25), .out26(decoder_1_out26), .out27(decoder_1_out27),
    .out28(decoder_1_out28), .out29(decoder_1_out29), .out30(decoder_1_out30), .out31(decoder_1_out31),
    .sel(Write_Reg));  // open: en
  and and_1 (and_1_out, RegWrite, decoder_1_out0);
  and and_2 (and_2_out, RegWrite, decoder_1_out1);
  and and_3 (and_3_out, RegWrite, decoder_1_out2);
  and and_4 (and_4_out, RegWrite, decoder_1_out3);
  and and_5 (and_5_out, RegWrite, decoder_1_out4);
  and and_6 (and_6_out, RegWrite, decoder_1_out5);
  and and_7 (and_7_out, RegWrite, decoder_1_out6);
  and and_8 (and_8_out, RegWrite, decoder_1_out7);
  and and_9 (and_9_out, RegWrite, decoder_1_out8);
  and and_10 (and_10_out, RegWrite, decoder_1_out9);
  and and_11 (and_11_out, RegWrite, decoder_1_out10);
  and and_12 (and_12_out, RegWrite, decoder_1_out11);
  and and_13 (and_13_out, RegWrite, decoder_1_out12);
  and and_14 (and_14_out, RegWrite, decoder_1_out13);
  and and_15 (and_15_out, RegWrite, decoder_1_out14);
  and and_16 (and_16_out, RegWrite, decoder_1_out15);
  and and_17 (and_17_out, RegWrite, decoder_1_out16);
  and and_18 (and_18_out, RegWrite, decoder_1_out17);
  and and_19 (and_19_out, RegWrite, decoder_1_out18);
  and and_20 (and_20_out, RegWrite, decoder_1_out19);
  and and_21 (and_21_out, RegWrite, decoder_1_out20);
  and and_22 (and_22_out, RegWrite, decoder_1_out21);
  and and_23 (and_23_out, RegWrite, decoder_1_out22);
  and and_24 (and_24_out, RegWrite, decoder_1_out23);
  and and_25 (and_25_out, RegWrite, decoder_1_out24);
  and and_26 (and_26_out, RegWrite, decoder_1_out25);
  and and_27 (and_27_out, RegWrite, decoder_1_out26);
  and and_28 (and_28_out, RegWrite, decoder_1_out27);
  and and_29 (and_29_out, RegWrite, decoder_1_out28);
  and and_30 (and_30_out, RegWrite, decoder_1_out29);
  and and_31 (and_31_out, RegWrite, decoder_1_out30);
  and and_32 (and_32_out, RegWrite, decoder_1_out31);
  Register #(.width(32)) zero (.en(and_1_out), .Q(zero_q), .clk(Clock), .clr(Clock));  // open: D
  Register #(.width(32)) at (.D(Write_Data), .en(and_2_out), .Q(at_q), .clk(Clock));  // open: clr
  Register #(.width(32)) v0 (.D(Write_Data), .en(and_3_out), .Q(v0_q), .clk(Clock));  // open: clr
  Register #(.width(32)) v1 (.D(Write_Data), .en(and_4_out), .Q(v1_q), .clk(Clock));  // open: clr
  Register #(.width(32)) a0 (.D(Write_Data), .en(and_5_out), .Q(a0_q), .clk(Clock));  // open: clr
  Register #(.width(32)) a1 (.D(Write_Data), .en(and_6_out), .Q(a1_q), .clk(Clock));  // open: clr
  Register #(.width(32)) a2 (.D(Write_Data), .en(and_7_out), .Q(a2_q), .clk(Clock));  // open: clr
  Register #(.width(32)) a3 (.D(Write_Data), .en(and_8_out), .Q(a3_q), .clk(Clock));  // open: clr
  Register #(.width(32)) t0 (.D(Write_Data), .en(and_9_out), .Q(t0_q), .clk(Clock));  // open: clr
  Register #(.width(32)) t1 (.D(Write_Data), .en(and_10_out), .Q(t1_q), .clk(Clock));  // open: clr
  Register #(.width(32)) t2 (.D(Write_Data), .en(and_11_out), .Q(t2_q), .clk(Clock));  // open: clr
  Register #(.width(32)) t3 (.D(Write_Data), .en(and_12_out), .Q(t3_q), .clk(Clock));  // open: clr
  Register #(.width(32)) t4 (.D(Write_Data), .en(and_13_out), .Q(t4_q), .clk(Clock));  // open: clr
  Register #(.width(32)) t5 (.D(Write_Data), .en(and_14_out), .Q(t5_q), .clk(Clock));  // open: clr
  Register #(.width(32)) t6 (.D(Write_Data), .en(and_15_out), .Q(t6_q), .clk(Clock));  // open: clr
  Register #(.width(32)) t7 (.D(Write_Data), .en(and_16_out), .Q(t7_q), .clk(Clock));  // open: clr
  Register #(.width(32)) s0 (.D(Write_Data), .en(and_17_out), .Q(s0_q), .clk(Clock));  // open: clr
  Register #(.width(32)) s1 (.D(Write_Data), .en(and_18_out), .Q(s1_q), .clk(Clock));  // open: clr
  Register #(.width(32)) s2 (.D(Write_Data), .en(and_19_out), .Q(s2_q), .clk(Clock));  // open: clr
  Register #(.width(32)) s3 (.D(Write_Data), .en(and_20_out), .Q(s3_q), .clk(Clock));  // open: clr
  Register #(.width(32)) s4 (.D(Write_Data), .en(and_21_out), .Q(s4_q), .clk(Clock));  // open: clr
  Register #(.width(32)) s5 (.D(Write_Data), .en(and_22_out), .Q(s5_q), .clk(Clock));  // open: clr
  Register #(.width(32)) s6 (.D(Write_Data), .en(and_23_out), .Q(s6_q), .clk(Clock));  // open: clr
  Register #(.width(32)) s7 (.D(Write_Data), .en(and_24_out), .Q(s7_q), .clk(Clock));  // open: clr
  Register #(.width(32)) t8 (.D(Write_Data), .en(and_25_out), .Q(t8_q), .clk(Clock));  // open: clr
  Register #(.width(32)) t9 (.D(Write_Data), .en(and_26_out), .Q(t9_q), .clk(Clock));  // open: clr
  Register #(.width(32)) k0 (.D(Write_Data), .en(and_27_out), .Q(k0_q), .clk(Clock));  // open: clr
  Register #(.width(32)) k1 (.D(Write_Data), .en(and_28_out), .Q(k1_q), .clk(Clock));  // open: clr
  Register #(.width(32)) gp (.D(Write_Data), .en(and_29_out), .Q(gp_q), .clk(Clock));  // open: clr
  Register #(.width(32)) sp (.D(Write_Data), .en(and_30_out), .Q(sp_q), .clk(Clock));  // open: clr
  Register #(.width(32)) fp (.D(Write_Data), .en(and_31_out), .Q(fp_q), .clk(Clock));  // open: clr
  Register #(.width(32)) ra (.D(Write_Data), .en(and_32_out), .Q(ra_q), .clk(Clock));  // open: clr
  Multiplexer #(.select(5), .width(32)) multiplexer_1 (
    .in0(zero_q), .in1(at_q), .in2(v0_q), .in3(v1_q), .in4(a0_q), .in5(a1_q), .in6(a2_q), .in7(a3_q),
    .in8(t0_q), .in9(t1_q), .in10(t2_q), .in11(t3_q), .in12(t4_q), .in13(t5_q), .in14(t6_q), .in15(t7_q),
    .in16(s0_q), .in17(s1_q), .in18(s2_q), .in19(s3_q), .in20(s4_q), .in21(s5_q), .in22(s6_q), .in23(s7_q),
    .in24(t8_q), .in25(t9_q), .in26(k0_q), .in27(k1_q), .in28(gp_q), .in29(sp_q), .in30(fp_q), .in31(ra_q),
    .out(Src_A), .sel(Reg_1));  // open: en
  Multiplexer #(.select(5), .width(32)) multiplexer_2 (
    .in0(zero_q), .in1(at_q), .in2(v0_q), .in3(v1_q), .in4(a0_q), .in5(a1_q), .in6(a2_q), .in7(a3_q),
    .in8(t0_q), .in9(t1_q), .in10(t2_q), .in11(t3_q), .in12(t4_q), .in13(t5_q), .in14(t6_q), .in15(t7_q),
    .in16(s0_q), .in17(s1_q), .in18(s2_q), .in19(s3_q), .in20(s4_q), .in21(s5_q), .in22(s6_q), .in23(s7_q),
    .in24(t8_q), .in25(t9_q), .in26(k0_q), .in27(k1_q), .in28(gp_q), .in29(sp_q), .in30(fp_q), .in31(ra_q),
    .out(Src_B), .sel(Reg_2));  // open: en
endmodule

module ALU_Control (
  input  [1:0] ALUOp,
  input  [4:0] Func,
  output [2:0] AluControl
);

  wire and_1_out, not_1_out, not_2_out, or_1_out;

  or or_1 (or_1_out, Func[0], Func[3]);
  and and_1 (and_1_out, ALUOp[1], Func[1]);
  and and_2 (AluControl[0], ALUOp[1], or_1_out);
  or or_2 (AluControl[2], ALUOp[0], and_1_out);
  not not_1 (not_1_out, ALUOp[1]);
  or or_3 (AluControl[1], not_1_out, not_2_out);
  not not_2 (not_2_out, Func[2]);
endmodule

module _32_bit_ALU_32x1 (
  input  in_1,
  input  [2:0] in_2,
  input  [31:0] in_3,
  input  [31:0] in_4,
  output [31:0] out_5,
  output out_6,
  output out_7,
  output out_8
);

  wire _0th_bit_out_7, _1st_bit_out_7, _4th_bit_out_7, _9th_bit_out_7, _13th_bit_out_7, _17th_bit_out_7,
       _21st_bit_out_7, _25th_bit_out_7, _29th_bit_out_7, n1_bit_alu_1_out_7, n1_bit_alu_2_out_7,
       n1_bit_alu_3_out_7, n1_bit_alu_4_out_7, n1_bit_alu_5_out_7, n1_bit_alu_6_out_7, n1_bit_alu_7_out_7,
       n1_bit_alu_8_out_7, n1_bit_alu_9_out_7, n1_bit_alu_10_out_7, n1_bit_alu_11_out_7, n1_bit_alu_12_out_7,
       n1_bit_alu_13_out_7, n1_bit_alu_14_out_7, n1_bit_alu_15_out_7, n1_bit_alu_16_out_7,
       n1_bit_alu_17_out_7, n1_bit_alu_18_out_7, n1_bit_alu_19_out_7, n1_bit_alu_20_out_7,
       n1_bit_alu_21_out_7, n1_bit_alu_22_out_7;

  _1_bit_ALU _0th_bit (
    .Less(out_8), .out_6(out_5[0]), .B(in_3[0]), .A(in_4[0]), .out_7(_0th_bit_out_7), .in_4(in_2),
    .Carry_In(in_2[2]));  // open: Set
  _1_bit_ALU _1st_bit (
    .Less(in_1), .out_6(out_5[1]), .B(in_3[1]), .A(in_4[1]), .out_7(_1st_bit_out_7), .in_4(in_2),
    .Carry_In(_0th_bit_out_7));  // open: Set
  _1_bit_ALU u_1_bit_alu_1 (
    .Less(in_1), .out_6(out_5[2]), .B(in_3[2]), .A(in_4[2]), .out_7(n1_bit_alu_1_out_7), .in_4(in_2),
    .Carry_In(_1st_bit_out_7));  // open: Set
  _1_bit_ALU u_1_bit_alu_2 (
    .Less(in_1), .out_6(out_5[3]), .B(in_3[3]), .A(in_4[3]), .out_7(n1_bit_alu_2_out_7), .in_4(in_2),
    .Carry_In(n1_bit_alu_1_out_7));  // open: Set
  _1_bit_ALU _4th_bit (
    .Less(in_1), .out_6(out_5[4]), .B(in_3[4]), .A(in_4[4]), .out_7(_4th_bit_out_7), .in_4(in_2),
    .Carry_In(n1_bit_alu_2_out_7));  // open: Set
  _1_bit_ALU u_1_bit_alu_3 (
    .Less(in_1), .out_6(out_5[5]), .B(in_3[5]), .A(in_4[5]), .out_7(n1_bit_alu_3_out_7), .in_4(in_2),
    .Carry_In(_4th_bit_out_7));  // open: Set
  _1_bit_ALU u_1_bit_alu_4 (
    .Less(in_1), .out_6(out_5[6]), .B(in_3[6]), .A(in_4[6]), .out_7(n1_bit_alu_4_out_7), .in_4(in_2),
    .Carry_In(n1_bit_alu_3_out_7));  // open: Set
  _1_bit_ALU u_1_bit_alu_5 (
    .Less(in_1), .out_6(out_5[7]), .B(in_3[7]), .A(in_4[7]), .out_7(n1_bit_alu_5_out_7), .in_4(in_2),
    .Carry_In(n1_bit_alu_4_out_7));  // open: Set
  _1_bit_ALU u_1_bit_alu_6 (
    .Less(in_1), .out_6(out_5[8]), .B(in_3[8]), .A(in_4[8]), .out_7(n1_bit_alu_6_out_7), .in_4(in_2),
    .Carry_In(n1_bit_alu_5_out_7));  // open: Set
  _1_bit_ALU _9th_bit (
    .Less(in_1), .out_6(out_5[9]), .B(in_3[9]), .A(in_4[9]), .out_7(_9th_bit_out_7), .in_4(in_2),
    .Carry_In(n1_bit_alu_6_out_7));  // open: Set
  _1_bit_ALU u_1_bit_alu_7 (
    .Less(in_1), .out_6(out_5[10]), .B(in_3[10]), .A(in_4[10]), .out_7(n1_bit_alu_7_out_7), .in_4(in_2),
    .Carry_In(_9th_bit_out_7));  // open: Set
  _1_bit_ALU u_1_bit_alu_8 (
    .Less(in_1), .out_6(out_5[11]), .B(in_3[11]), .A(in_4[11]), .out_7(n1_bit_alu_8_out_7), .in_4(in_2),
    .Carry_In(n1_bit_alu_7_out_7));  // open: Set
  _1_bit_ALU u_1_bit_alu_9 (
    .Less(in_1), .out_6(out_5[12]), .B(in_3[12]), .A(in_4[12]), .out_7(n1_bit_alu_9_out_7), .in_4(in_2),
    .Carry_In(n1_bit_alu_8_out_7));  // open: Set
  _1_bit_ALU _13th_bit (
    .Less(in_1), .out_6(out_5[13]), .B(in_3[13]), .A(in_4[13]), .out_7(_13th_bit_out_7), .in_4(in_2),
    .Carry_In(n1_bit_alu_9_out_7));  // open: Set
  _1_bit_ALU u_1_bit_alu_10 (
    .Less(in_1), .out_6(out_5[14]), .B(in_3[14]), .A(in_4[14]), .out_7(n1_bit_alu_10_out_7), .in_4(in_2),
    .Carry_In(_13th_bit_out_7));  // open: Set
  _1_bit_ALU u_1_bit_alu_11 (
    .Less(in_1), .out_6(out_5[15]), .B(in_3[15]), .A(in_4[15]), .out_7(n1_bit_alu_11_out_7), .in_4(in_2),
    .Carry_In(n1_bit_alu_10_out_7));  // open: Set
  _1_bit_ALU u_1_bit_alu_12 (
    .Less(in_1), .out_6(out_5[16]), .B(in_3[16]), .A(in_4[16]), .out_7(n1_bit_alu_12_out_7), .in_4(in_2),
    .Carry_In(n1_bit_alu_11_out_7));  // open: Set
  _1_bit_ALU _17th_bit (
    .Less(in_1), .out_6(out_5[17]), .B(in_3[17]), .A(in_4[17]), .out_7(_17th_bit_out_7), .in_4(in_2),
    .Carry_In(n1_bit_alu_12_out_7));  // open: Set
  _1_bit_ALU u_1_bit_alu_13 (
    .Less(in_1), .out_6(out_5[18]), .B(in_3[18]), .A(in_4[18]), .out_7(n1_bit_alu_13_out_7), .in_4(in_2),
    .Carry_In(_17th_bit_out_7));  // open: Set
  _1_bit_ALU u_1_bit_alu_14 (
    .Less(in_1), .out_6(out_5[19]), .B(in_3[19]), .A(in_4[19]), .out_7(n1_bit_alu_14_out_7), .in_4(in_2),
    .Carry_In(n1_bit_alu_13_out_7));  // open: Set
  _1_bit_ALU u_1_bit_alu_15 (
    .Less(in_1), .out_6(out_5[20]), .B(in_3[20]), .A(in_4[20]), .out_7(n1_bit_alu_15_out_7), .in_4(in_2),
    .Carry_In(n1_bit_alu_14_out_7));  // open: Set
  _1_bit_ALU _21st_bit (
    .Less(in_1), .out_6(out_5[21]), .B(in_3[21]), .A(in_4[21]), .out_7(_21st_bit_out_7), .in_4(in_2),
    .Carry_In(n1_bit_alu_15_out_7));  // open: Set
  _1_bit_ALU u_1_bit_alu_16 (
    .Less(in_1), .out_6(out_5[22]), .B(in_3[22]), .A(in_4[22]), .out_7(n1_bit_alu_16_out_7), .in_4(in_2),
    .Carry_In(_21st_bit_out_7));  // open: Set
  _1_bit_ALU u_1_bit_alu_17 (
    .Less(in_1), .out_6(out_5[23]), .B(in_3[23]), .A(in_4[23]), .out_7(n1_bit_alu_17_out_7), .in_4(in_2),
    .Carry_In(n1_bit_alu_16_out_7));  // open: Set
  _1_bit_ALU u_1_bit_alu_18 (
    .Less(in_1), .out_6(out_5[24]), .B(in_3[24]), .A(in_4[24]), .out_7(n1_bit_alu_18_out_7), .in_4(in_2),
    .Carry_In(n1_bit_alu_17_out_7));  // open: Set
  _1_bit_ALU _25th_bit (
    .Less(in_1), .out_6(out_5[25]), .B(in_3[25]), .A(in_4[25]), .out_7(_25th_bit_out_7), .in_4(in_2),
    .Carry_In(n1_bit_alu_18_out_7));  // open: Set
  _1_bit_ALU u_1_bit_alu_19 (
    .Less(in_1), .out_6(out_5[26]), .B(in_3[26]), .A(in_4[26]), .out_7(n1_bit_alu_19_out_7), .in_4(in_2),
    .Carry_In(_25th_bit_out_7));  // open: Set
  _1_bit_ALU u_1_bit_alu_20 (
    .Less(in_1), .out_6(out_5[27]), .B(in_3[27]), .A(in_4[27]), .out_7(n1_bit_alu_20_out_7), .in_4(in_2),
    .Carry_In(n1_bit_alu_19_out_7));  // open: Set
  _1_bit_ALU u_1_bit_alu_21 (
    .Less(in_1), .out_6(out_5[28]), .B(in_3[28]), .A(in_4[28]), .out_7(n1_bit_alu_21_out_7), .in_4(in_2),
    .Carry_In(n1_bit_alu_20_out_7));  // open: Set
  _1_bit_ALU _29th_bit (
    .Less(in_1), .out_6(out_5[29]), .B(in_3[29]), .A(in_4[29]), .out_7(_29th_bit_out_7), .in_4(in_2),
    .Carry_In(n1_bit_alu_21_out_7));  // open: Set
  _1_bit_ALU u_1_bit_alu_22 (
    .Less(in_1), .out_6(out_5[30]), .B(in_3[30]), .A(in_4[30]), .out_7(n1_bit_alu_22_out_7), .in_4(in_2),
    .Carry_In(_29th_bit_out_7));  // open: Set
  _1_bit_ALU _31st_bit (
    .Less(in_1), .out_6(out_5[31]), .B(in_3[31]), .A(in_4[31]), .out_7(out_7), .Set(out_8), .in_4(in_2),
    .Carry_In(n1_bit_alu_22_out_7));
  nor nor_1 (out_6, out_5[0], out_5[1], out_5[2], out_5[3], out_5[4], out_5[5], out_5[6], out_5[7], out_5[8], out_5[9], out_5[10], out_5[11], out_5[12], out_5[13], out_5[14], out_5[15], out_5[16], out_5[17], out_5[18], out_5[19], out_5[20], out_5[21], out_5[22], out_5[23], out_5[24], out_5[25], out_5[26], out_5[27], out_5[28], out_5[29], out_5[30], out_5[31]);

  // Notes on the sheet:
  //   24-31
  //   16-23
  //   8-15
  //   0-7
endmodule

module Next_PC (
  input  [29:0] Inc_PC,
  input  beq,
  input  bne,
  input  [25:0] Imm_26,
  input  jump,
  input  zero,
  output [29:0] Target_Address,
  output PCSrc
);

  wire and_1_out, and_2_out, not_1_out;
  wire [15:0] bit_extender_1_out;
  wire [29:0] adder_1_out, bit_extender_2_out;

  Bit_Extender #(.in_width(26)) bit_extender_1 (.in(Imm_26), .out(bit_extender_1_out));
  assign bit_extender_2_out = {{14{bit_extender_1_out[15]}}, bit_extender_1_out};  // Bit_Extender bit_extender_2
  Adder #(.width(30)) adder_1 (.a(Inc_PC), .b(bit_extender_2_out), .out(adder_1_out));  // open: cin, cout
  Multiplexer #(.width(30)) multiplexer_1 (
    .in0(adder_1_out), .in1({Imm_26, Inc_PC[3:0]}), .out(Target_Address), .sel(jump));  // open: en
  or or_1 (PCSrc, and_1_out, jump, and_2_out);
  and and_1 (and_1_out, not_1_out, bne);
  not not_1 (not_1_out, zero);
  and and_2 (and_2_out, zero, beq);
endmodule
